# Fritzing sketch fritzing (saved by Fritzing 0.9.3b)

parts:
  Componente1 = Arduino Uno (Rev3)
  Part1 = KY-037 High Sensitivity Sound Detection Module [package="Breakout board"]
  U1 = Module 4 Relais 5V [package="Module 4 Relais 5V"]
  LED3 = LEDs [package=led10mm]

nets:
  GND: Componente1.GND, Part1.G, U1.GND
  N1: Componente1.D3_PWM, Part1.D0
  N2: Componente1.D7, U1.IN2
  N3: Componente1.5V, Part1.+
  N4: U1.K4-Com, LED3.C

custom parts:
  KY-037 High Sensitivity Sound Detection Module: KY-037 high sensitivity sound detection module is an analog/digital sensor that uses a condenser microphone to observe changes in environment noise.
  Module 4 Relais 5V: Module 4 Relais 5V 4x SPD-06VDC-SD-C
  LEDs: LEDs Standard schematic elements and footprints for 5mm, 3mm, 1206, and 0603 sized LEDs. 5mm - Spark Fun Electronics SKU : COM-00529 (and others)
